# Fritzing sketch mock_flash_zaurus (saved by Fritzing 1.0.3b)
circuit board: 5cm x 5.4cm
breadboards: 1

parts:
  U1 = WS2812 RGB LED strip
  J1 = Piezo Speaker
  パーツ1 = Arduino Uno (Rev3)
  S2 = Pushbutton [package="[THT]"]

nets:
  GND: U1.GND, J1.pin1, パーツ1.GND, S2.Pin_3, S2.Pin_4
  5V: U1.VCC, パーツ1.5V
  N1: U1.DIN, パーツ1.D6_PWM
  N2: J1.pin2, パーツ1.D11_PWM/MOSI
  N3: パーツ1.D4, S2.Pin_1, S2.Pin_2

custom parts:
  WS2812 RGB LED strip: WS2812 strip
